// Logisim project 3BitGrayCodeCounterUsingFkFlipFlop.circ as structural Verilog: 1 circuit, main circuit main
module main (
  input  in_1
);

  wire and_1_out, and_2_out, and_3_out, and_4_out, j_k_ff_1_q, j_k_ff_1_qn, j_k_ff_2_q, j_k_ff_2_qn,
       j_k_ff_3_q, j_k_ff_3_qn, xnor_1_out, xor_1_out;

  xnor xnor_1 (xnor_1_out, j_k_ff_2_q, j_k_ff_3_q);
  xor xor_1 (xor_1_out, j_k_ff_2_q, j_k_ff_3_q);
  J_K_Flip_Flop j_k_ff_1 (
    .J(xnor_1_out), .clk(in_1), .K(xor_1_out), .Q(j_k_ff_1_q), .Qn(j_k_ff_1_qn));  // open: preset, en, reset
  and and_1 (and_1_out, j_k_ff_1_q, j_k_ff_3_qn);
  and and_2 (and_2_out, j_k_ff_1_q, j_k_ff_3_q);
  J_K_Flip_Flop j_k_ff_2 (
    .J(and_1_out), .clk(in_1), .K(and_2_out), .Q(j_k_ff_2_q), .Qn(j_k_ff_2_qn));  // open: preset, en, reset
  and and_3 (and_3_out, j_k_ff_2_q, j_k_ff_1_qn);
  and and_4 (and_4_out, j_k_ff_1_qn, j_k_ff_2_qn);
  J_K_Flip_Flop j_k_ff_3 (
    .J(and_3_out), .clk(in_1), .K(and_4_out), .Q(j_k_ff_3_q), .Qn(j_k_ff_3_qn));  // open: preset, en, reset

  // Notes on the sheet:
  //   0
  //   1
  //   2
endmodule
